// Logisim project RAM.circ as structural Verilog: 1 circuit, main circuit main
module main (
  input  [7:0] D,
  input  Clk,
  input  En,
  input  [2:0] Addr,
  output [7:0] out_5
);

  wire decoder_1_out0, decoder_1_out1, decoder_1_out2, decoder_1_out3, decoder_1_out4, decoder_1_out5,
       decoder_1_out6, decoder_1_out7;
  wire [7:0] multiplexer_1_out, multiplexer_2_out, multiplexer_3_out, multiplexer_4_out, multiplexer_5_out,
       multiplexer_6_out, register_1_q, register_2_q, register_3_q, register_4_q, register_5_q, register_6_q,
       register_7_q, register_8_q;

  Decoder #(.select(3)) decoder_1 (
    .out0(decoder_1_out0), .out1(decoder_1_out1), .out2(decoder_1_out2), .out3(decoder_1_out3),
    .out4(decoder_1_out4), .out5(decoder_1_out5), .out6(decoder_1_out6), .out7(decoder_1_out7), .sel(Addr),
    .en(En));
  Register register_1 (.D(D), .en(decoder_1_out0), .clk(Clk), .Q(register_1_q));  // open: clr
  Register register_2 (.D(D), .en(decoder_1_out1), .clk(Clk), .Q(register_2_q));  // open: clr
  Register register_3 (.D(D), .en(decoder_1_out2), .clk(Clk), .Q(register_3_q));  // open: clr
  Register register_4 (.D(D), .en(decoder_1_out3), .clk(Clk), .Q(register_4_q));  // open: clr
  Register register_5 (.D(D), .en(decoder_1_out4), .clk(Clk), .Q(register_5_q));  // open: clr
  Register register_6 (.D(D), .en(decoder_1_out5), .clk(Clk), .Q(register_6_q));  // open: clr
  Register register_7 (.D(D), .en(decoder_1_out6), .clk(Clk), .Q(register_7_q));  // open: clr
  Register register_8 (.D(D), .en(decoder_1_out7), .clk(Clk), .Q(register_8_q));  // open: clr
  Multiplexer #(.width(8)) multiplexer_1 (
    .in0(register_1_q), .in1(register_2_q), .out(multiplexer_1_out), .sel(Addr[0]));
  Multiplexer #(.width(8)) multiplexer_2 (
    .in0(register_3_q), .in1(register_4_q), .out(multiplexer_2_out), .sel(Addr[0]));
  Multiplexer #(.width(8)) multiplexer_3 (
    .in0(register_5_q), .in1(register_6_q), .out(multiplexer_3_out), .sel(Addr[0]));
  Multiplexer #(.width(8)) multiplexer_4 (
    .in0(register_7_q), .in1(register_8_q), .out(multiplexer_4_out), .sel(Addr[0]));
  Multiplexer #(.width(8)) multiplexer_5 (
    .in0(multiplexer_1_out), .in1(multiplexer_2_out), .out(multiplexer_5_out), .sel(Addr[1]));
  Multiplexer #(.width(8)) multiplexer_6 (
    .in0(multiplexer_3_out), .in1(multiplexer_4_out), .out(multiplexer_6_out), .sel(Addr[1]));
  Multiplexer #(.width(8)) multiplexer_7 (.in0(multiplexer_5_out), .in1(multiplexer_6_out), .out(out_5), .sel(Addr[2]));

  // Other names for the same wires on the sheet: S_0 = Addr[0]; S_1 = Addr[1]; S_2 = Addr[2]
endmodule
