// Logisim project ROMwithMUX.circ as structural Verilog: 1 circuit, main circuit main
module main (
  input  [2:0] Addr,
  output [7:0] out_2
);

  wire [7:0] multiplexer_1_out, multiplexer_2_out, multiplexer_3_out, multiplexer_4_out, multiplexer_5_out,
       multiplexer_6_out, register_1_q, register_2_q, register_3_q, register_4_q, register_5_q, register_6_q,
       register_7_q, register_8_q;

  Register register_1 (.Q(register_1_q));  // open: D, en, clk, clr
  Register register_2 (.Q(register_2_q));  // open: D, en, clk, clr
  Register register_3 (.Q(register_3_q));  // open: D, en, clk, clr
  Register register_4 (.Q(register_4_q));  // open: D, en, clk, clr
  Register register_5 (.Q(register_5_q));  // open: D, en, clk, clr
  Register register_6 (.Q(register_6_q));  // open: D, en, clk, clr
  Register register_7 (.Q(register_7_q));  // open: D, en, clk, clr
  Register register_8 (.Q(register_8_q));  // open: D, en, clk, clr
  Multiplexer #(.width(8)) multiplexer_1 (
    .in0(register_1_q), .in1(register_2_q), .out(multiplexer_1_out), .sel(Addr[0]));
  Multiplexer #(.width(8)) multiplexer_2 (
    .in0(register_3_q), .in1(register_4_q), .out(multiplexer_2_out), .sel(Addr[0]));
  Multiplexer #(.width(8)) multiplexer_3 (
    .in0(register_5_q), .in1(register_6_q), .out(multiplexer_3_out), .sel(Addr[0]));
  Multiplexer #(.width(8)) multiplexer_4 (
    .in0(register_7_q), .in1(register_8_q), .out(multiplexer_4_out), .sel(Addr[0]));
  Multiplexer #(.width(8)) multiplexer_5 (
    .in0(multiplexer_1_out), .in1(multiplexer_2_out), .out(multiplexer_5_out), .sel(Addr[1]));
  Multiplexer #(.width(8)) multiplexer_6 (
    .in0(multiplexer_3_out), .in1(multiplexer_4_out), .out(multiplexer_6_out), .sel(Addr[1]));
  Multiplexer #(.width(8)) multiplexer_7 (.in0(multiplexer_5_out), .in1(multiplexer_6_out), .out(out_2), .sel(Addr[2]));

  // Other names for the same wires on the sheet: S_0 = Addr[0]; S_1 = Addr[1]; S_2 = Addr[2]
endmodule
