// Logisim project sCPU.circ as structural Verilog: 1 circuit, main circuit main
module main (
  output [7:0] out_1
);

  wire clock_1_out, clock_2_out, comparator_1_gt, comparator_1_lt, decoder_1_out0, decoder_1_out2,
       decoder_2_out0, decoder_2_out1, decoder_2_out2, decoder_2_out3, Inst_bner0, or_1_out, or_2_out,
       pc_load, Reset;
  wire [1:0] imm, opcode;
  wire [3:0] addr;
  wire [7:0] adder_1_out, bit_extender_1_out, bit_extender_2_out, counter_1_q, r0_data, R1_q, R2_q, R3_q,
       rs1_data, rs2_data;

  Clock clock_1 (.out(clock_1_out));
  assign bit_extender_1_out = {{4{1'b0}}, addr};  // Bit_Extender bit_extender_1
  Button button_1 (.out(Reset));
  Counter counter_1 (
    .clr(Reset), .load(pc_load), .clk(clock_1_out), .D(bit_extender_1_out), .Q(counter_1_q));  // open: up, count, carry
  assign bit_extender_2_out = {{4{1'b0}}, {addr[1:0], imm}};  // Bit_Extender bit_extender_2
  Decoder #(.select(2)) decoder_1 (
    .out0(decoder_1_out0), .out2(decoder_1_out2), .out3(Inst_bner0), .sel(opcode));  // open: out1, en
  Decoder #(.select(2)) decoder_2 (
    .out0(decoder_2_out0), .out1(decoder_2_out1), .out2(decoder_2_out2), .out3(decoder_2_out3),
    .sel(addr[3:2]), .en(or_1_out));
  Adder adder_1 (.a(rs1_data), .b(rs2_data), .out(adder_1_out));  // open: cin, cout
  Multiplexer #(.width(8)) multiplexer_1 (
    .in0(adder_1_out), .in1(bit_extender_2_out), .out(out_1), .sel(decoder_1_out2));
  or or_1 (or_1_out, decoder_1_out0, decoder_1_out2);
  ROM rom_1 (.addr(counter_1_q), .data({opcode, addr, imm}));
  Clock clock_2 (.out(clock_2_out));
  Comparator comparator_1 (.a(r0_data), .b(rs2_data), .gt(comparator_1_gt), .lt(comparator_1_lt));  // open: eq
  Register R0 (.D(out_1), .en(decoder_2_out0), .clk(clock_2_out), .Q(r0_data), .clr(Reset));
  Register R1 (.D(out_1), .en(decoder_2_out1), .clk(clock_2_out), .Q(R1_q), .clr(Reset));
  Register R2 (.D(out_1), .en(decoder_2_out2), .clk(clock_2_out), .Q(R2_q), .clr(Reset));
  Register R3 (.D(out_1), .en(decoder_2_out3), .clk(clock_2_out), .Q(R3_q), .clr(Reset));
  or or_2 (or_2_out, comparator_1_gt, comparator_1_lt);
  and and_1 (pc_load, or_2_out, Inst_bner0);
  Multiplexer #(.select(2), .width(8)) multiplexer_2 (
    .in0(r0_data), .in1(R1_q), .in2(R2_q), .in3(R3_q), .out(rs1_data), .sel(addr[1:0]));
  Multiplexer #(.select(2), .width(8)) multiplexer_3 (
    .in0(r0_data), .in1(R1_q), .in2(R2_q), .in3(R3_q), .out(rs2_data), .sel(imm));

  // Other names for the same wires on the sheet: imm[3:2] = addr[1:0]; rs1[1:0] = addr[1:0]; rd[1:0] = addr[3:2];
  //   rs2[1:0] = imm

  // Notes on the sheet:
  //   add
  //   li
  //   contents of rom_1 (hex, n*v repeats v):
  //   8a 90 a0 b1 17 29 d1 df
  //   数列求和要运行10次，最后结果储存在R2中，16进制为37，十进制为55
  //   10001010    # 0: li r0, 10 
  //   10010000    # 1: li r1, 0 
  //   10100000    # 2: li r2, 0 
  //   10110001    # 3: li r3, 1 
  //   00010111    # 4: add r1, r1, r3 
  //   00101001    # 5: add r2, r2, r1 
  //   11010001    # 6: bner0 r1, 4 
  //   11011111    # 7: bner0 r3, 7 
  //   8A
  //   90
  //   A0
  //   B1
  //   17
  //   29
  //   D1
  //   DF
endmodule
