// Logisim project sCPU_only_li.circ as structural Verilog: 1 circuit, main circuit main
module main (
  output [3:0] out_1,
  output [3:0] out_2,
  output [3:0] out_3
);

  wire button_1_out, clock_1_out, clock_2_out, decoder_1_out0, decoder_1_out1, decoder_1_out2,
       decoder_1_out3, nand_1_out;
  wire [1:0] OP_code, Rd;
  wire [3:0] multiplexer_1_out, multiplexer_2_out, R0_q, R2_q, R3_q;
  wire [7:0] counter_1_q;

  Button button_1 (.out(button_1_out));
  Clock clock_1 (.out(clock_1_out));
  Counter counter_1 (.clr(button_1_out), .clk(clock_1_out), .Q(counter_1_q));  // open: load, up, count, D, carry
  nand nand_1 (nand_1_out, OP_code[0], OP_code[1]);
  Decoder #(.select(2)) decoder_1 (
    .out0(decoder_1_out0), .out1(decoder_1_out1), .out2(decoder_1_out2), .out3(decoder_1_out3), .sel(Rd),
    .en(nand_1_out));
  ROM rom_1 (.addr(counter_1_q), .data({OP_code, Rd, out_1}));
  Clock clock_2 (.out(clock_2_out));
  Register #(.width(4)) R0 (.D(out_1), .en(decoder_1_out0), .clk(clock_2_out), .Q(R0_q));  // open: clr
  Register #(.width(4)) R1 (.D(out_1), .en(decoder_1_out1), .clk(clock_2_out), .Q(out_2));  // open: clr
  Register #(.width(4)) R2 (.D(out_1), .en(decoder_1_out2), .clk(clock_2_out), .Q(R2_q));  // open: clr
  Register #(.width(4)) R3 (.D(out_1), .en(decoder_1_out3), .clk(clock_2_out), .Q(R3_q));  // open: clr
  Multiplexer #(.width(4)) multiplexer_1 (.in0(R0_q), .in1(out_2), .out(multiplexer_1_out), .sel(Rd[0]));
  Multiplexer #(.width(4)) multiplexer_2 (.in0(R2_q), .in1(R3_q), .out(multiplexer_2_out), .sel(Rd[0]));
  Multiplexer #(.width(4)) multiplexer_3 (.in0(multiplexer_1_out), .in1(multiplexer_2_out), .out(out_3), .sel(Rd[1]));

  // Other names for the same wires on the sheet: imm[3:0] = out_1; S_0 = Rd[0]; S_1 = Rd[1]

  // Notes on the sheet:
  //   只有li指令
  //   contents of rom_1 (hex, n*v repeats v):
  //   12 15 16
endmodule
