// Logisim project minirv.circ as structural Verilog: 1 circuit, main circuit main
module main (
  output [11:0] out_1
);

  wire add, addi, clock_1_out, clock_2_out, clock_3_out, comparator_1_eq, comparator_2_eq, comparator_3_eq,
       comparator_4_eq, comparator_5_eq, comparator_6_eq, comparator_7_eq, comparator_9_eq, comparator_10_eq,
       comparator_11_eq, comparator_12_eq, comparator_13_eq, comparator_14_eq, comparator_15_eq,
       comparator_16_eq, CTR_write_en, decoder_1_out1, decoder_1_out2, decoder_1_out3, decoder_1_out4,
       decoder_1_out5, decoder_1_out6, decoder_1_out7, decoder_1_out8, decoder_1_out9, decoder_1_out10,
       decoder_1_out11, decoder_1_out12, decoder_1_out13, decoder_1_out14, decoder_1_out15, decoder_2_out0,
       decoder_2_out1, decoder_2_out2, decoder_2_out3, lbu, lui, lw, RAM_BE0, RAM_BE1, RAM_BE2, RAM_BE3,
       RAM_WE, Reset, sb, sw, write_R;
  wire [1:0] bit_extender_3_out;
  wire [2:0] funct3;
  wire [3:0] bit_extender_1_out, rs1, rs2;
  wire [4:0] ibu_byte_select, imm_Stype, multiplier_1_out, multiplier_2_out, sb_byte_select;
  wire [6:0] opcode;
  wire [7:3] imm_Utype;
  wire [23:0] bit_extender_2_out, bit_extender_6_out;
  wire [31:0] adder_1_out, adder_2_out, adder_3_out, adder_4_out, adder_5_out, adder_6_out, adder_7_out,
       adder_8_out, and_8_out, and_9_out, and_10_out, bit_extender_7_out, bit_extender_8_out,
       bit_extender_9_out, bit_extender_10_out, bit_extender_11_out, bit_extender_12_out, new_PC_data,
       PC_data, RAM_data, RAM_mem_adress, register_1_q, register_2_q, register_3_q, register_4_q,
       register_5_q, register_6_q, register_7_q, register_8_q, register_9_q, register_10_q, register_11_q,
       register_12_q, register_13_q, register_14_q, register_15_q, register_16_q, rs1_data, rs2_data,
       shifter_1_out, shifter_2_out, shifter_3_out, shifter_4_out, shifter_5_out, shifter_6_out,
       shifter_7_out, shifter_8_out, write_data, write_mem_data;

  Button button_1 (.out(Reset));
  Clock clock_1 (.out(clock_1_out));
  // Probe on new_PC_data
  Counter #(.max('hffffffff), .width(32)) counter_1 (
    .clr(Reset), .load(CTR_write_en), .clk(clock_1_out), .D(new_PC_data), .Q(PC_data));  // open: up, count, carry
  // Probe on bit_extender_1_out
  Bit_Extender #(.in_width(5), .out_width(4), .\type ("zero")) bit_extender_1 (
    .in(imm_Stype), .out(bit_extender_1_out));
  Decoder #(.select(4)) decoder_1 (
    .out1(decoder_1_out1), .out2(decoder_1_out2), .out3(decoder_1_out3), .out4(decoder_1_out4),
    .out5(decoder_1_out5), .out6(decoder_1_out6), .out7(decoder_1_out7), .out8(decoder_1_out8),
    .out9(decoder_1_out9), .out10(decoder_1_out10), .out11(decoder_1_out11), .out12(decoder_1_out12),
    .out13(decoder_1_out13), .out14(decoder_1_out14), .out15(decoder_1_out15), .sel(bit_extender_1_out),
    .en(write_R));  // open: out0
  or or_1 (write_R, addi, CTR_write_en, lui, lbu, lw);
  // Probe on write_data
  Clock clock_2 (.out(clock_2_out));
  Register #(.width(32)) register_1 (.D(write_data), .en(1'b0), .clk(clock_2_out), .Q(register_1_q), .clr(Reset));
  Register #(.width(32)) register_2 (
    .D(write_data), .en(decoder_1_out8), .clk(clock_2_out), .Q(register_2_q), .clr(Reset));
  Bit_Extender #(.in_width(32), .out_width(24), .\type ("zero")) bit_extender_2 (
    .in(PC_data), .out(bit_extender_2_out));
  // Probe on PC_data
  Register #(.width(32)) register_3 (
    .D(write_data), .en(decoder_1_out1), .clk(clock_2_out), .Q(register_3_q), .clr(Reset));
  Register #(.width(32)) register_4 (
    .D(write_data), .en(decoder_1_out9), .clk(clock_2_out), .Q(register_4_q), .clr(Reset));
  ROM #(.addrWidth(24), .dataWidth(32)) rom_1 (
    .addr(bit_extender_2_out), .data({out_1, imm_Utype, funct3, imm_Stype, opcode}));
  or or_2 (RAM_WE, sw, sb);
  Register #(.width(32)) register_5 (
    .D(write_data), .en(decoder_1_out2), .clk(clock_2_out), .Q(register_5_q), .clr(Reset));
  Register #(.width(32)) register_6 (
    .D(write_data), .en(decoder_1_out10), .clk(clock_2_out), .Q(register_6_q), .clr(Reset));
  Register #(.width(32)) register_7 (
    .D(write_data), .en(decoder_1_out3), .clk(clock_2_out), .Q(register_7_q), .clr(Reset));
  Register #(.width(32)) register_8 (
    .D(write_data), .en(decoder_1_out11), .clk(clock_2_out), .Q(register_8_q), .clr(Reset));
  Register #(.width(32)) register_9 (
    .D(write_data), .en(decoder_1_out4), .clk(clock_2_out), .Q(register_9_q), .clr(Reset));
  Register #(.width(32)) register_10 (
    .D(write_data), .en(decoder_1_out12), .clk(clock_2_out), .Q(register_10_q), .clr(Reset));
  Register #(.width(32)) register_11 (
    .D(write_data), .en(decoder_1_out5), .clk(clock_2_out), .Q(register_11_q), .clr(Reset));
  Register #(.width(32)) register_12 (
    .D(write_data), .en(decoder_1_out13), .clk(clock_2_out), .Q(register_12_q), .clr(Reset));
  Bit_Extender #(.in_width(5), .out_width(2), .\type ("zero")) bit_extender_3 (
    .in(sb_byte_select), .out(bit_extender_3_out));
  Register #(.width(32)) register_13 (
    .D(write_data), .en(decoder_1_out6), .clk(clock_2_out), .Q(register_13_q), .clr(Reset));
  Register #(.width(32)) register_14 (
    .D(write_data), .en(decoder_1_out14), .clk(clock_2_out), .Q(register_14_q), .clr(Reset));
  Decoder #(.select(2)) decoder_2 (
    .out0(decoder_2_out0), .out1(decoder_2_out1), .out2(decoder_2_out2), .out3(decoder_2_out3),
    .sel(bit_extender_3_out), .en(sb));
  Register #(.width(32)) register_15 (
    .D(write_data), .en(decoder_1_out7), .clk(clock_2_out), .Q(register_15_q), .clr(Reset));
  Register #(.width(32)) register_16 (
    .D(write_data), .en(decoder_1_out15), .clk(clock_2_out), .Q(register_16_q), .clr(Reset));
  Bit_Extender #(.in_width(5), .out_width(4), .\type ("zero")) bit_extender_4 (.in(imm_Utype), .out(rs1));
  Bit_Extender #(.in_width(5), .out_width(4), .\type ("zero")) bit_extender_5 (.in(out_1[4:0]), .out(rs2));
  or or_3 (RAM_BE0, sw, decoder_2_out0);
  or or_4 (RAM_BE1, sw, decoder_2_out1);
  or or_5 (RAM_BE2, sw, decoder_2_out2);
  or or_6 (RAM_BE3, sw, decoder_2_out3);
  // Probe on shifter_1_out
  Clock clock_3 (.out(clock_3_out));
  Shifter #(.shift("lr"), .width(32)) shifter_1 (.in(RAM_mem_adress), .\dist (5'b00010), .out(shifter_1_out));
  // Probe on write_mem_data
  Multiplexer #(.select(4), .width(32)) multiplexer_1 (
    .in0(register_1_q), .in1(register_3_q), .in2(register_5_q), .in3(register_7_q), .in4(register_9_q),
    .in5(register_11_q), .in6(register_13_q), .in7(register_15_q), .in8(register_2_q), .in9(register_4_q),
    .in10(register_6_q), .in11(register_8_q), .in12(register_10_q), .in13(register_12_q),
    .in14(register_14_q), .in15(register_16_q), .out(rs1_data), .sel(rs1));
  Multiplexer #(.select(4), .width(32)) multiplexer_2 (
    .in0(register_1_q), .in1(register_3_q), .in2(register_5_q), .in3(register_7_q), .in4(register_9_q),
    .in5(register_11_q), .in6(register_13_q), .in7(register_15_q), .in8(register_2_q), .in9(register_4_q),
    .in10(register_6_q), .in11(register_8_q), .in12(register_10_q), .in13(register_12_q),
    .in14(register_14_q), .in15(register_16_q), .out(rs2_data), .sel(rs2));
  // Probe on bit_extender_6_out
  RAM #(.addrWidth(24), .asyncread("true"), .byteenables("byteEnables"), .dataWidth(32), .\type ("nonvolatile")) ram_1 (
    .addr(bit_extender_6_out), .we(RAM_WE), .oe(1'b1), .clk(clock_3_out), .din(write_mem_data),
    .dout(RAM_data), .be3(RAM_BE3), .be2(RAM_BE2), .be1(RAM_BE1), .be0(RAM_BE0));
  Bit_Extender #(.in_width(32), .out_width(24), .\type ("zero")) bit_extender_6 (
    .in(shifter_1_out), .out(bit_extender_6_out));
  assign bit_extender_7_out = {{20{1'b0}}, out_1};  // Bit_Extender bit_extender_7
  // Probe on rs1_data
  assign bit_extender_8_out = {{20{1'b0}}, out_1};  // Bit_Extender bit_extender_8
  // Probe on bit_extender_8_out
  Adder #(.width(32)) adder_1 (.a(PC_data), .b(32'h1), .out(adder_1_out));  // open: cin, cout
  Shifter #(.width(32)) shifter_2 (.in(adder_1_out), .\dist (5'b00010), .out(shifter_2_out));
  Adder #(.width(32)) adder_2 (.a(rs1_data), .b(bit_extender_7_out), .out(adder_2_out));  // open: cin, cout
  Adder #(.width(32)) adder_3 (.a(rs1_data), .b(bit_extender_8_out), .out(adder_3_out));  // open: cin, cout
  assign write_data = CTR_write_en ? shifter_2_out : 32'bz;  // Controlled_Buffer controlled_buffer_1
  // Probe on write_data
  assign write_data = addi ? adder_2_out : 32'bz;  // Controlled_Buffer controlled_buffer_2
  Shifter #(.shift("lr"), .width(32)) shifter_3 (.in(adder_3_out), .\dist (5'b00001), .out(shifter_3_out));
  Comparator #(.mode("unsigned"), .width(7)) comparator_1 (
    .a(7'b0010011), .b(opcode), .eq(comparator_1_eq));  // open: gt, lt
  Comparator #(.mode("unsigned"), .width(3)) comparator_2 (
    .a(3'b000), .b(funct3), .eq(comparator_2_eq));  // open: gt, lt
  Comparator #(.mode("unsigned"), .width(7)) comparator_3 (
    .a(7'b1100111), .b(opcode), .eq(comparator_3_eq));  // open: gt, lt
  Comparator #(.mode("unsigned"), .width(3)) comparator_4 (
    .a(3'b000), .b(funct3), .eq(comparator_4_eq));  // open: gt, lt
  Comparator #(.mode("unsigned"), .width(7)) comparator_5 (
    .a(7'b0110011), .b(opcode), .eq(comparator_5_eq));  // open: gt, lt
  Comparator #(.mode("unsigned"), .width(3)) comparator_6 (
    .a(3'b000), .b(funct3), .eq(comparator_6_eq));  // open: gt, lt
  Comparator #(.mode("unsigned"), .width(7)) comparator_7 (
    .a({7{1'b0}}), .b(out_1[11:5]), .eq(comparator_7_eq));  // open: gt, lt
  Comparator #(.mode("unsigned"), .width(7)) comparator_8 (.a(7'b0110111), .b(opcode), .eq(lui));  // open: gt, lt
  Comparator #(.mode("unsigned"), .width(7)) comparator_9 (
    .a(7'b0000011), .b(opcode), .eq(comparator_9_eq));  // open: gt, lt
  Comparator #(.mode("unsigned"), .width(3)) comparator_10 (
    .a(3'b010), .b(funct3), .eq(comparator_10_eq));  // open: gt, lt
  Comparator #(.mode("unsigned"), .width(7)) comparator_11 (
    .a(7'b0000011), .b(opcode), .eq(comparator_11_eq));  // open: gt, lt
  Comparator #(.mode("unsigned"), .width(3)) comparator_12 (
    .a(3'b100), .b(funct3), .eq(comparator_12_eq));  // open: gt, lt
  Comparator #(.mode("unsigned"), .width(7)) comparator_13 (
    .a(7'b0100011), .b(opcode), .eq(comparator_13_eq));  // open: gt, lt
  Comparator #(.mode("unsigned"), .width(3)) comparator_14 (
    .a(3'b010), .b(funct3), .eq(comparator_14_eq));  // open: gt, lt
  Comparator #(.mode("unsigned"), .width(7)) comparator_15 (
    .a(7'b0100011), .b(opcode), .eq(comparator_15_eq));  // open: gt, lt
  Comparator #(.mode("unsigned"), .width(3)) comparator_16 (
    .a(3'b000), .b(funct3), .eq(comparator_16_eq));  // open: gt, lt
  Shifter #(.width(32)) shifter_4 (.in(shifter_3_out), .\dist (5'b00001), .out(shifter_4_out));
  Shifter #(.shift("lr"), .width(32)) shifter_5 (.in(shifter_4_out), .\dist (5'b00010), .out(shifter_5_out));
  and and_1 (addi, comparator_1_eq, comparator_2_eq);
  and and_2 (CTR_write_en, comparator_3_eq, comparator_4_eq);
  and and_3 (add, comparator_5_eq, comparator_6_eq, comparator_7_eq);
  and and_4 (lw, comparator_9_eq, comparator_10_eq);
  and and_5 (lbu, comparator_11_eq, comparator_12_eq);
  and and_6 (sw, comparator_13_eq, comparator_14_eq);
  and and_7 (sb, comparator_15_eq, comparator_16_eq);
  // Probe on new_PC_data
  assign new_PC_data = CTR_write_en ? shifter_5_out : 32'bz;  // Controlled_Buffer controlled_buffer_3
  assign bit_extender_9_out = {{20{1'b0}}, out_1};  // Bit_Extender bit_extender_9
  assign bit_extender_10_out = {{20{1'b0}}, out_1};  // Bit_Extender bit_extender_10
  Multiplier #(.width(5)) multiplier_1 (.a(ibu_byte_select), .b(5'b01000), .out(multiplier_1_out));  // open: cin, cout
  assign write_mem_data = sw ? rs2_data : 32'bz;  // Controlled_Buffer controlled_buffer_4
  assign bit_extender_11_out = {{20{1'b0}}, {out_1[11:5], imm_Stype}};  // Bit_Extender bit_extender_11
  assign bit_extender_12_out = {{20{1'b0}}, {out_1[11:5], imm_Stype}};  // Bit_Extender bit_extender_12
  Adder #(.width(32)) adder_4 (.a(rs1_data), .b(rs2_data), .out(adder_4_out));  // open: cin, cout
  Adder #(.width(32)) adder_5 (.a(rs1_data), .b(bit_extender_9_out), .out(adder_5_out));  // open: cin, cout
  assign write_data = lw ? RAM_data : 32'bz;  // Controlled_Buffer controlled_buffer_5
  Adder #(.width(32)) adder_6 (.a(rs1_data), .b(bit_extender_10_out), .out(adder_6_out));  // open: cin, cout
  assign and_8_out = RAM_mem_adress & 32'h3;  // AND_Gate and_8, 32 bits wide
  // Probe on rs2_data
  Multiplier #(.width(5)) multiplier_2 (.a(sb_byte_select), .b(5'b01000), .out(multiplier_2_out));  // open: cin, cout
  // Probe on write_data
  assign write_data = add ? adder_4_out : 32'bz;  // Controlled_Buffer controlled_buffer_6
  assign write_data = lui ? {out_1, imm_Utype, funct3, {12{1'b0}}} : 32'bz;  // Controlled_Buffer controlled_buffer_7
  // Probe on RAM_mem_adress
  assign RAM_mem_adress = lw ? adder_5_out : 32'bz;  // Controlled_Buffer controlled_buffer_8
  // Probe on RAM_mem_adress
  assign RAM_mem_adress = lbu ? adder_6_out : 32'bz;  // Controlled_Buffer controlled_buffer_9
  assign and_9_out = RAM_mem_adress & 32'h3;  // AND_Gate and_9, 32 bits wide
  Shifter #(.width(32)) shifter_6 (.in(32'hff), .\dist (multiplier_1_out), .out(shifter_6_out));
  assign RAM_mem_adress = sw ? adder_7_out : 32'bz;  // Controlled_Buffer controlled_buffer_10
  Adder #(.width(32)) adder_7 (.a(rs1_data), .b(bit_extender_11_out), .out(adder_7_out));  // open: cin, cout
  Adder #(.width(32)) adder_8 (.a(rs1_data), .b(bit_extender_12_out), .out(adder_8_out));  // open: cin, cout
  // Probe on sb_byte_select
  Bit_Extender #(.in_width(32), .out_width(5), .\type ("zero")) bit_extender_13 (.in(and_8_out), .out(sb_byte_select));
  // Probe on multiplier_2_out
  Bit_Extender #(.in_width(32), .out_width(5), .\type ("zero")) bit_extender_14 (.in(and_9_out), .out(ibu_byte_select));
  assign and_10_out = RAM_data & shifter_6_out;  // AND_Gate and_10, 32 bits wide
  // Probe on RAM_mem_adress
  assign RAM_mem_adress = sb ? adder_8_out : 32'bz;  // Controlled_Buffer controlled_buffer_11
  // Probe on shifter_7_out
  Shifter #(.width(32)) shifter_7 (.in(rs2_data), .\dist (multiplier_2_out), .out(shifter_7_out));
  Shifter #(.shift("lr"), .width(32)) shifter_8 (.in(and_10_out), .\dist (multiplier_1_out), .out(shifter_8_out));
  assign write_mem_data = sb ? shifter_7_out : 32'bz;  // Controlled_Buffer controlled_buffer_12
  assign write_data = lbu ? shifter_8_out : 32'bz;  // Controlled_Buffer controlled_buffer_13

  // Other names for the same wires on the sheet: imm_Utype (some bits) = {out_1, funct3}; imm_Itype[11:0] = out_1;
  //   funct7[6:0] = out_1[11:5]; imm_Stype[11:5] = out_1[11:5]; rd[4:0] = imm_Stype; jalr = CTR_write_en

  // Notes on the sheet:
  //   0号寄存器把0写死
  //   zero
  //   contents of rom_1 (hex, n*v repeats v):
  //   2083 4103 102223 100423 100623
  //   ra
  //   a0
  //   寄存器按字节存储，Pc中的指令按字存储
  //   Addi
  //   jalr
  //   寄存器的数据右移2位成pc中的地址，pc中的左移2位存到寄存器中
  //   Operation
  //   sw
  //   Add
  //   lui
  //   lw
  //   lbu
  //   sb
endmodule
