// Logisim project minirv_onlytwo.circ as structural Verilog: 1 circuit, main circuit main
module main (
  output [11:0] out_1
);

  wire addi, clock_1_out, clock_2_out, comparator_1_eq, comparator_2_eq, comparator_3_eq, comparator_4_eq,
       CTR_write_en, decoder_1_out1, decoder_1_out2, decoder_1_out3, decoder_1_out4, decoder_1_out5,
       decoder_1_out6, decoder_1_out7, decoder_1_out8, decoder_1_out9, decoder_1_out10, decoder_1_out11,
       decoder_1_out12, decoder_1_out13, decoder_1_out14, decoder_1_out15, Reset, write_en;
  wire [2:0] funct3;
  wire [3:0] bit_extender_1_out, rs1, rs2;
  wire [4:0] imm_Stype_0_4;
  wire [6:0] opcode;
  wire [7:3] imm_Utype_12_31;
  wire [23:0] bit_extender_2_out;
  wire [31:0] adder_1_out, adder_2_out, adder_3_out, bit_extender_5_out, bit_extender_6_out, new_PC_data,
       PC_data, register_1_q, register_2_q, register_3_q, register_4_q, register_5_q, register_6_q,
       register_7_q, register_8_q, register_9_q, register_10_q, register_11_q, register_12_q, register_13_q,
       register_14_q, register_15_q, register_16_q, rs1_data, rs2_data, shifter_1_out, shifter_2_out,
       shifter_3_out, shifter_4_out, write_data;

  Clock clock_1 (.out(clock_1_out));
  // Probe on new_PC_data
  Counter #(.max('hffffffff), .width(32)) counter_1 (
    .clr(Reset), .load(CTR_write_en), .clk(clock_1_out), .D(new_PC_data), .Q(PC_data));  // open: up, count, carry
  Bit_Extender #(.in_width(5), .out_width(4), .\type ("zero")) bit_extender_1 (
    .in(imm_Stype_0_4), .out(bit_extender_1_out));
  // Probe on PC_data
  Button button_1 (.out(Reset));
  // Probe on write_data
  Decoder #(.select(4)) decoder_1 (
    .out1(decoder_1_out1), .out2(decoder_1_out2), .out3(decoder_1_out3), .out4(decoder_1_out4),
    .out5(decoder_1_out5), .out6(decoder_1_out6), .out7(decoder_1_out7), .out8(decoder_1_out8),
    .out9(decoder_1_out9), .out10(decoder_1_out10), .out11(decoder_1_out11), .out12(decoder_1_out12),
    .out13(decoder_1_out13), .out14(decoder_1_out14), .out15(decoder_1_out15), .sel(bit_extender_1_out),
    .en(write_en));  // open: out0
  ROM #(.addrWidth(24), .dataWidth(32)) rom_1 (
    .addr(bit_extender_2_out), .data({out_1, imm_Utype_12_31, funct3, imm_Stype_0_4, opcode}));
  Bit_Extender #(.in_width(32), .out_width(24), .\type ("zero")) bit_extender_2 (
    .in(PC_data), .out(bit_extender_2_out));
  Clock clock_2 (.out(clock_2_out));
  Register #(.width(32)) register_1 (.D(write_data), .en(1'b0), .clk(clock_2_out), .Q(register_1_q), .clr(Reset));
  Register #(.width(32)) register_2 (
    .D(write_data), .en(decoder_1_out8), .clk(clock_2_out), .Q(register_2_q), .clr(Reset));
  Register #(.width(32)) register_3 (
    .D(write_data), .en(decoder_1_out1), .clk(clock_2_out), .Q(register_3_q), .clr(Reset));
  Register #(.width(32)) register_4 (
    .D(write_data), .en(decoder_1_out9), .clk(clock_2_out), .Q(register_4_q), .clr(Reset));
  or or_1 (write_en, addi, CTR_write_en);
  Register #(.width(32)) register_5 (
    .D(write_data), .en(decoder_1_out2), .clk(clock_2_out), .Q(register_5_q), .clr(Reset));
  Register #(.width(32)) register_6 (
    .D(write_data), .en(decoder_1_out10), .clk(clock_2_out), .Q(register_6_q), .clr(Reset));
  Register #(.width(32)) register_7 (
    .D(write_data), .en(decoder_1_out3), .clk(clock_2_out), .Q(register_7_q), .clr(Reset));
  Register #(.width(32)) register_8 (
    .D(write_data), .en(decoder_1_out11), .clk(clock_2_out), .Q(register_8_q), .clr(Reset));
  Register #(.width(32)) register_9 (
    .D(write_data), .en(decoder_1_out4), .clk(clock_2_out), .Q(register_9_q), .clr(Reset));
  Register #(.width(32)) register_10 (
    .D(write_data), .en(decoder_1_out12), .clk(clock_2_out), .Q(register_10_q), .clr(Reset));
  Register #(.width(32)) register_11 (
    .D(write_data), .en(decoder_1_out5), .clk(clock_2_out), .Q(register_11_q), .clr(Reset));
  Register #(.width(32)) register_12 (
    .D(write_data), .en(decoder_1_out13), .clk(clock_2_out), .Q(register_12_q), .clr(Reset));
  Register #(.width(32)) register_13 (
    .D(write_data), .en(decoder_1_out6), .clk(clock_2_out), .Q(register_13_q), .clr(Reset));
  Register #(.width(32)) register_14 (
    .D(write_data), .en(decoder_1_out14), .clk(clock_2_out), .Q(register_14_q), .clr(Reset));
  Bit_Extender #(.in_width(5), .out_width(4), .\type ("zero")) bit_extender_3 (.in(imm_Utype_12_31), .out(rs1));
  Bit_Extender #(.in_width(5), .out_width(4), .\type ("zero")) bit_extender_4 (.in(out_1[4:0]), .out(rs2));
  assign bit_extender_5_out = {{20{out_1[11]}}, out_1};  // Bit_Extender bit_extender_5
  // Probe on bit_extender_5_out
  Register #(.width(32)) register_15 (
    .D(write_data), .en(decoder_1_out7), .clk(clock_2_out), .Q(register_15_q), .clr(Reset));
  Register #(.width(32)) register_16 (
    .D(write_data), .en(decoder_1_out15), .clk(clock_2_out), .Q(register_16_q), .clr(Reset));
  assign bit_extender_6_out = {{20{out_1[11]}}, out_1};  // Bit_Extender bit_extender_6
  // Probe on rs1_data
  Adder #(.width(32)) adder_1 (.a(PC_data), .b(32'h1), .out(adder_1_out));  // open: cin, cout
  Adder #(.width(32)) adder_2 (.a(rs1_data), .b(bit_extender_6_out), .out(adder_2_out));  // open: cin, cout
  Adder #(.width(32)) adder_3 (.a(rs1_data), .b(bit_extender_5_out), .out(adder_3_out));  // open: cin, cout
  assign write_data = CTR_write_en ? shifter_1_out : 32'bz;  // Controlled_Buffer controlled_buffer_1
  Shifter #(.width(32)) shifter_1 (.in(adder_1_out), .\dist (5'b00010), .out(shifter_1_out));
  // Probe on write_data
  assign write_data = addi ? adder_2_out : 32'bz;  // Controlled_Buffer controlled_buffer_2
  Shifter #(.shift("lr"), .width(32)) shifter_2 (.in(adder_3_out), .\dist (5'b00001), .out(shifter_2_out));
  Shifter #(.width(32)) shifter_3 (.in(shifter_2_out), .\dist (5'b00001), .out(shifter_3_out));
  Multiplexer #(.select(4), .width(32)) multiplexer_1 (
    .in0(register_1_q), .in1(register_3_q), .in2(register_5_q), .in3(register_7_q), .in4(register_9_q),
    .in5(register_11_q), .in6(register_13_q), .in7(register_15_q), .in8(register_2_q), .in9(register_4_q),
    .in10(register_6_q), .in11(register_8_q), .in12(register_10_q), .in13(register_12_q),
    .in14(register_14_q), .in15(register_16_q), .out(rs1_data), .sel(rs1));
  Multiplexer #(.select(4), .width(32)) multiplexer_2 (
    .in0(register_1_q), .in1(register_3_q), .in2(register_5_q), .in3(register_7_q), .in4(register_9_q),
    .in5(register_11_q), .in6(register_13_q), .in7(register_15_q), .in8(register_2_q), .in9(register_4_q),
    .in10(register_6_q), .in11(register_8_q), .in12(register_10_q), .in13(register_12_q),
    .in14(register_14_q), .in15(register_16_q), .out(rs2_data), .sel(rs2));
  Comparator #(.mode("unsigned"), .width(7)) comparator_1 (
    .a(7'b0010011), .b(opcode), .eq(comparator_1_eq));  // open: gt, lt
  Comparator #(.mode("unsigned"), .width(3)) comparator_2 (
    .a(3'b000), .b(funct3), .eq(comparator_2_eq));  // open: gt, lt
  Comparator #(.mode("unsigned"), .width(7)) comparator_3 (
    .a(7'b1100111), .b(opcode), .eq(comparator_3_eq));  // open: gt, lt
  Comparator #(.mode("unsigned"), .width(3)) comparator_4 (
    .a(3'b000), .b(funct3), .eq(comparator_4_eq));  // open: gt, lt
  // Probe on new_PC_data
  assign new_PC_data = CTR_write_en ? shifter_4_out : 32'bz;  // Controlled_Buffer controlled_buffer_3
  Shifter #(.shift("lr"), .width(32)) shifter_4 (.in(shifter_3_out), .\dist (5'b00010), .out(shifter_4_out));
  and and_1 (addi, comparator_1_eq, comparator_2_eq);
  and and_2 (CTR_write_en, comparator_3_eq, comparator_4_eq);

  // Other names for the same wires on the sheet: rd[4:0] = imm_Stype_0_4; imm_Itype[11:0] = out_1;
  //   imm_Utype_12_31 (some bits) = {out_1, funct3}; funct7[6:0] = out_1[11:5]; imm_Stype_5_11[6:0] = out_1[11:5];
  //   jalr = CTR_write_en

  // Notes on the sheet:
  //   contents of rom_1 (hex, n*v repeats v):
  //   1400513 10000e7 c000e7 c00067 a50513 8067
  //   0号寄存器把0写死
  //   zero
  //   ra
  //   a0
  //   寄存器按字节存储，Pc中的指令按字存储
  //   Add
  //   jalr
  //   寄存器的数据右移2位成pc中的地址，pc中的左移2位存到寄存器中
  //   Operation
endmodule
